# Fritzing sketch HDD Power (saved by Fritzing 0.8.7b)

parts:
  Part1 = Arduino Uno (Rev3)
  Serial_Port_L1 = DIODE-SCHOTTKY [package=sma-diode]
  Remote = DIODE-SCHOTTKY [package=sma-diode]
  Optocoupler = Optocoupler [package=THT]

nets:
  N1: Part1.A0, Serial_Port_L1.C
  N2: Part1.GND, Serial_Port_L1.A, Remote.D, Optocoupler.Pin_2
  N3: Part1.D2, Optocoupler.Pin_1
  N4: Part1.D3_PWM, Remote.B
  N5: Remote.A, Optocoupler.Pin_5
  N6: Remote.C, Optocoupler.Pin_4

notes:
  4 lead wire
  Coaxial cable

custom parts:
  DIODE-SCHOTTKY: Commonly MBRA140.
