# Fritzing sketch console board v2 (saved by Fritzing 0.9.3b)
perfboards: 1

parts:
  J1 = screw terminal, 8 pins  # not connected
  J2 = screw terminal, 8 pins  # not connected
  U1 = Sharp PC817 [package=THT]
  U2 = Sharp PC817 [package=THT]
  IC1 = Voltage Regulator [package=to-220-alt]
  R1 = Resistor [tolerance=±5% resistance=680 package=THT]
  R2 = Resistor [tolerance=±5% resistance=680 package=THT]
  U3 = RELAY [package=relay-g5q]  # not connected
  R3 = Resistor [tolerance=±5% resistance=680 package=THT]
  LED1 = LEDs [package=led10mm]
  TRS1 = Audio Jack (TRRS) 3.5mm [part_number="LUMBERG JEITA RC-5325A" package="RC-5325A [SMD]"]  # not connected

nets:
  N1: U1.Pin_1, R1.Pin_1
  N2: U1.Pin_3, IC1.GND
  N3: U2.Pin_1, R2.Pin_0
  N4: IC1.OUT, R3.Pin_1
  N5: R3.Pin_0, LED1.A

notes:
  from head unit
  to cd changer
  switch
  led
  usb
  aux in
  GND
  12V
  ACC
  L
  R
  BUS
