# Fritzing sketch Motorcontroller Circut Diag (saved by Fritzing 0.8.7b)
breadboards: 1

parts:
  LCD1 = LCD screen  # not connected
  Initiate_Spool = Pushbutton [package="[THT]"]
  Speed_Control = Trimmer Potentiometer [maximum_resistance=10kΩ package=THT]
  Screen_I/O = Trimmer Potentiometer [maximum_resistance=10kΩ package=THT]  # not connected

nets:
  N1: Initiate_Spool.Pin_1, Initiate_Spool.Pin_2, Speed_Control.wiper
  N2: Initiate_Spool.Pin_3, Initiate_Spool.Pin_4
