# Fritzing sketch console board (saved by Fritzing 0.8.7b)
circuit board: 8.46667cm x 5.64444cm
perfboards: 1

parts:
  U1 = TLP621 [package=THT]
  R1 = Resistor [tolerance=±5% resistance=680 package=THT]  # not connected
  U2 = TLP621 [package=THT]
  R2 = Resistor [tolerance=±5% resistance=680 package=THT]
  R3 = Resistor [tolerance=±5% resistance=680 package=THT]  # not connected
  U3 = AUDIO-JACK2 [package=audio-jack-3.5mm-smd]
  R4 = Resistor [tolerance=±5% resistance=1M package=THT]
  R5 = Resistor [tolerance=±5% resistance=47k package=THT]  # not connected
  R6 = Resistor [tolerance=±5% resistance=47k package=THT]  # not connected

nets:
  N1: U1.Pin_3, U2.Pin_4
  N2: U2.Pin_1, R2.Pin_1
  N3: U3.TSH, R4.Pin_0

notes:
  to glove box
  to cd changer
  from head unit
  switch
  power led
  usb port
  ---------------------------------------------------------------------------
  aux in
  POWER
  AUDIO
  COM
  5V
  HIGH if aux plugged in
  *
  *note: needs to be connected to
  arduino gnd as well as audio gnd
